# Fritzing sketch push-button-protoboard (saved by Fritzing 0.9.3b)
breadboards: 1

parts:
  Componente1 = Arduino Uno (Rev3)
  S1 = Pushbutton [package="[SMD]"]

nets:
  N1: Componente1.D13/SCK, S1.Pin_3, S1.Pin_4
  N2: Componente1.GND, S1.Pin_1, S1.Pin_2
